// Logisim project Cache.circ as structural Verilog: 9 circuits, main circuit main
module main (
  input  EnableTestHalting,
  output [9:0] CorrectCounter,
  output [9:0] HitCounter,
  output [9:0] MissCounter,
  output [9:0] TestNumber,
  output [7:0] ByteRead,
  output [7:0] CorrectByteRead,
  output Halt
);

  wire and_3_out, and_4_out, and_5_out, CLK, CmdIsRead, Correct, CpuRead, CpuWrite, DidContain, HaltTesting,
       MaxItersReached, MemRead, MemWrite, not_1_out, not_2_out, not_4_out, NotDoneTesting, Ok2Count,
       or_1_out, Ready;
  wire [7:0] CpuWriteValue, MemAddress;
  wire [9:0] CpuAddress;
  wire [31:0] Line2Mem, LineFromMem;

  not not_1 (not_1_out, Ready);
  Clock clock_1 (.out(CLK));
  or or_1 (or_1_out, MaxItersReached, Ready);
  Counter #(.width(4), .max('h9)) MaxClocks (
    .load(Ready), .D(4'b0001), .count(not_1_out), .carry(MaxItersReached), .clk(CLK));  // open: Q, clr
  and and_1 (HaltTesting, EnableTestHalting, CmdIsRead, not_2_out);
  not not_2 (not_2_out, Correct);
  not not_3 (NotDoneTesting, Halt);
  Inputs inputs_1 (
    .HaltTesting(HaltTesting), .Ready(or_1_out), .CLK(CLK), .Done(Halt), .Read(CpuRead), .Write(CpuWrite),
    .Address(CpuAddress), .Value(CpuWriteValue), .TestNumber(TestNumber));
  Cache cache_1 (
    .CpuAddress(CpuAddress), .CpuRead(CpuRead), .CpuWrite(CpuWrite), .CpuWriteValue(CpuWriteValue),
    .CLK(CLK), .Ready(Ready), .DidContain(DidContain), .ByteRead(ByteRead), .MemAddress(MemAddress),
    .MemRead(MemRead), .MemWrite(MemWrite), .LineFromMem(LineFromMem), .Line2Mem(Line2Mem));
  // Probe on CpuRead
  // Probe on CpuWrite
  // Probe on CpuAddress
  // Probe on CpuWriteValue
  // Probe on TestNumber
  // Probe on CorrectByteRead
  // Probe on Correct
  // Probe on Ready
  // Probe on DidContain
  // Probe on ByteRead
  // Probe on MemAddress
  // Probe on MemRead
  // Probe on MemWrite
  // Probe on HitCounter
  // Probe on LineFromMem
  // Probe on Line2Mem
  not not_4 (not_4_out, HaltTesting);
  RAM #(.dataWidth(32), .bus("separate")) ram_1 (
    .addr(MemAddress), .din(Line2Mem), .data(LineFromMem), .str(MemWrite), .clk(CLK), .ld(MemRead));  // open: sel, clr
  and and_2 (Ok2Count, Ready, not_4_out, NotDoneTesting);
  and and_3 (and_3_out, Correct, Ok2Count);
  and and_4 (and_4_out, DidContain, Ok2Count);
  and and_5 (and_5_out, MemRead, NotDoneTesting);
  Checker checker_1 (
    .TestNumber(TestNumber), .YourByteRead(ByteRead), .CmdIsRead(CmdIsRead),
    .CorrectByteRead(CorrectByteRead), .Correct(Correct));
  Counter #(.width(10), .max('h3ff)) u_CorrectCounter (
    .count(and_3_out), .Q(CorrectCounter), .clk(CLK));  // open: load, D, carry, clr
  Counter #(.width(10), .max('h3ff)) u_HitCounter (
    .count(and_4_out), .Q(HitCounter), .clk(CLK));  // open: load, D, carry, clr
  Counter #(.width(10), .max('h3ff)) u_MissCounter (
    .count(and_5_out), .Q(MissCounter), .clk(CLK));  // open: load, D, carry, clr
  // Probe on CorrectCounter
  // Probe on HitCounter
  // Probe on MissCounter

  // Other names for the same wires on the sheet: DoneTesting = Halt

  // Notes on the sheet:
  //   Yifan Liu:915107182
  //   Angyu Lyu:914932002
  //   Your Answer Inside Here
endmodule

module Cache (
  input  [9:0] CpuAddress,
  input  CpuRead,
  input  CpuWrite,
  input  [7:0] CpuWriteValue,
  input  CLK,
  input  [31:0] LineFromMem,
  output Ready,
  output DidContain,
  output [7:0] ByteRead,
  output [7:0] MemAddress,
  output MemRead,
  output MemWrite,
  output [31:0] Line2Mem
);

  wire AgeIfEmpty, comparator_1_eq, ContainOne, ContainTwo, DirtyOne, DirtyTwo, IfAgeChange, IfContainPrev,
       IfDirty, IfDirtyChange, IfStore, IfTagChange, IfValidChange, multiplexer_2_out, NewDirty, NewValid,
       OneBegin, ReadEnabled, Set_One, Set_Two, TwoBegin, ValidOne, ValidTwo, Write, WriteEnabled;
  wire [1:0] Offset;
  wire [2:0] fsm_1_nextbit0, Step;
  wire [6:0] multiplexer_6_out, TagOne, TagTwo;
  wire [7:0] ByteOne, ByteTwo, WriteVal;
  wire [9:2] SavedCpuAdrr;
  wire [31:0] BlockOne, BlockTwo, LineFromMem_t;

  Register #(.width(10)) address (.D(CpuAddress), .en(IfStore), .Q({SavedCpuAdrr, Offset}), .clk(CLK));  // open: clr
  Register #(.width(1)) read (.D(CpuRead), .en(IfStore), .Q(ReadEnabled), .clk(CLK));  // open: clr
  Register #(.width(1)) u_write (.D(CpuWrite), .en(IfStore), .Q(WriteEnabled), .clk(CLK));  // open: clr
  Register u_writeVal (.D(CpuWriteValue), .en(IfStore), .Q(WriteVal), .clk(CLK));  // open: clr
  Comparator #(.width(1), .mode("unsigned")) comparator_1 (
    .a(SavedCpuAdrr[2]), .b(1'b0), .eq(comparator_1_eq));  // open: gt, lt
  not not_1 (Set_Two, Set_One);
  or or_1 (OneBegin, AgeIfEmpty, Set_One);
  or or_2 (TwoBegin, AgeIfEmpty, Set_Two);
  Multiplexer #(.enable("false")) multiplexer_1 (.in0(1'b0), .in1(1'b1), .out(Set_One), .sel(comparator_1_eq));
  sfm0 sfm0_1 (
    .BIT2(Step[2]), .BIT1(Step[1]), .BIT0(Step[0]), .Write(WriteEnabled), .Read(ReadEnabled),
    .Dirty(IfDirty), .Found(DidContain), .IfTagChange(IfTagChange), .IfValidChange(IfValidChange),
    .IfDirtyChange(IfDirtyChange), .write_2(Write), .newage(IfAgeChange));
  FSM fsm_1 (
    .BIT2(Step[2]), .BIT1(Step[1]), .BIT0(Step[0]), .Write(WriteEnabled), .Read(ReadEnabled),
    .Dirty(IfDirty), .Found(DidContain), .NextBit2(fsm_1_nextbit0[2]), .NextBit1(fsm_1_nextbit0[1]),
    .NextBit0(fsm_1_nextbit0[0]), .Ready(Ready), .AgeIfEmpty(AgeIfEmpty),
    .CheckIfContainPreviously(IfContainPrev), .ReadFromMemory(MemRead), .IfStore(IfStore),
    .Write2Mem(MemWrite), .NewValid(NewValid), .NewDirty(NewDirty));
  Multiplexer #(.enable("false")) multiplexer_2 (
    .in0(ContainOne), .in1(ContainTwo), .out(multiplexer_2_out), .sel(SavedCpuAdrr[2]));
  Multiplexer #(.enable("false")) multiplexer_3 (.in0(DirtyOne), .in1(DirtyTwo), .out(IfDirty), .sel(SavedCpuAdrr[2]));
  Multiplexer #(.width(32), .enable("false")) multiplexer_4 (
    .in0(BlockOne), .in1(BlockTwo), .out(Line2Mem), .sel(SavedCpuAdrr[2]));
  Multiplexer #(.width(8), .enable("false")) multiplexer_5 (
    .in0(ByteOne), .in1(ByteTwo), .out(ByteRead), .sel(SavedCpuAdrr[2]));
  Register #(.width(1)) u_DidContain (
    .D(multiplexer_2_out), .en(IfContainPrev), .Q(DidContain), .clk(CLK));  // open: clr
  Register #(.width(3)) State (.D(fsm_1_nextbit0), .en(1'b1), .Q(Step), .clk(CLK));  // open: clr
  Multiplexer #(.width(7), .enable("false")) multiplexer_6 (
    .in0(TagOne), .in1(TagTwo), .out(multiplexer_6_out), .sel(SavedCpuAdrr[2]));
  Set set_1 (
    .Begin(TwoBegin), .Tag(SavedCpuAdrr[9:3]), .Offset(Offset), .BlockFromMem(LineFromMem_t),
    .CPUWriteVal(WriteVal), .IsValid(NewValid), .IsDirty(NewDirty), .IfTagChange(IfTagChange),
    .IfValidChange(IfValidChange), .IfDirtyChange(IfDirtyChange), .IfAgeChange(IfAgeChange),
    .AgeIfEmpty(AgeIfEmpty), .Write(Write), .CLK(CLK), .UpdatedTag(TagTwo), .UpdatedBlock(BlockTwo),
    .UpdatedByteRead(ByteTwo), .UpdatedValid(ValidTwo), .UpdatedDirty(DirtyTwo), .DidContain(ContainTwo));
  Multiplexer #(.width(8), .enable("false")) multiplexer_7 (
    .in0(SavedCpuAdrr), .in1({multiplexer_6_out, SavedCpuAdrr[2]}), .out(MemAddress), .sel(MemWrite));
  Set set_2 (
    .Begin(OneBegin), .Tag(SavedCpuAdrr[9:3]), .Offset(Offset), .BlockFromMem(LineFromMem),
    .CPUWriteVal(WriteVal), .IsValid(NewValid), .IsDirty(NewDirty), .IfTagChange(IfTagChange),
    .IfValidChange(IfValidChange), .IfDirtyChange(IfDirtyChange), .IfAgeChange(IfAgeChange),
    .AgeIfEmpty(AgeIfEmpty), .Write(Write), .CLK(CLK), .UpdatedTag(TagOne), .UpdatedBlock(BlockOne),
    .UpdatedByteRead(ByteOne), .UpdatedValid(ValidOne), .UpdatedDirty(DirtyOne), .DidContain(ContainOne));

  // Other names for the same wires on the sheet: SetNumber = SavedCpuAdrr[2]; BlockFromMem[31:0] = LineFromMem;
  //   BlockToMem[31:0] = Line2Mem; IfFound = DidContain; MemAddr[7:0] = MemAddress; ReadFromMem = MemRead;
  //   SavedCpuAdrr[1:0] = Offset; Tag[6:0] = SavedCpuAdrr[9:3]; WriteToMem = MemWrite

  // Notes on the sheet:
  //   Address Bits = 10
  //   Line Size = 4
  //   W = 3
  //   Num Sets = 2
  //   C =4*3*2 = 24bytes
  //   Tag bits = 7
endmodule

module Inputs (
  input  HaltTesting,
  input  Ready,
  input  CLK,
  output Done,
  output Read,
  output Write,
  output [9:0] Address,
  output [7:0] Value,
  output [9:0] TestNumber
);

  wire and_1_out, not_1_out, not_2_out;

  not not_1 (not_1_out, HaltTesting);
  not not_2 (not_2_out, Done);
  Counter #(.width(10), .max('h3ff), .ongoal("stay")) u_TestNumber (
    .count(and_1_out), .Q(TestNumber), .clk(CLK));  // open: load, D, carry, clr
  and and_1 (and_1_out, not_1_out, Ready, not_2_out);
  ROM #(.addrWidth(10), .dataWidth(21)) rom_1 (
    .addr(TestNumber), .data({Done, Read, Write, Address, Value}));  // open: sel

  // Notes on the sheet:
  //   contents of rom_1 (hex, n*v repeats v):
  //   80882 83fe6 4306b 83e0e 43701 42275 8280f 80304 41bd8 84371 43f77 41d70 4250b 44733 8253d 440d8
  //   82691 440c9 83d7c 43558 446bf 83837 842c9 43e0f 4059d 41556 80166 833b0 43a89 83142 8361c 42e66
  //   43eb6 42c00 43a0e 8165c 84682 8092a 83907 41f89 817b0 40855 82056 425e8 43ff2 8039f 42bd7 82137
  //   4416b 40273 8324a 814e4 44570 41c0f 429da 82640 8069c 8099e 414d5 41004 81beb 84113 419b1 81add
  //   83f35 425ff 829cd 40250 82945 4366d 40cc2 444f8 80814 81156 8446d 42a82 42bae 82578 41135 405d0
  //   8304b 82b3a 40972 822ba 4443a 42337 82506 80bd3 80560 83552 83955 81434 43096 43da1 81aa2 80305
  //   428e6 428cc 808a2 40e80 845f0 4215d 82765 82e29 40be5 82b74 42715 417a2 41fab 8452f 81c0a 83325
  //   44624 80205 42dfc 41333 40958 81348 42736 41069 84510 44669 826dd 8067e 408e4 44680 444e8 832ad
  //   821f8 83509 82d46 81184 432cd 80b77 4005a 440e0 81ea0 43d73 42b8c 80624 41468 42699 415ed 80fc1 0
  //   100000
endmodule

module Checker (
  input  [9:0] TestNumber,
  input  [7:0] YourByteRead,
  output CmdIsRead,
  output [7:0] CorrectByteRead,
  output Correct
);

  wire comparator_1_eq;
  wire [9:0] subtractor_1_out;

  // Probe on TestNumber
  Subtractor #(.width(10)) subtractor_1 (.a(TestNumber), .b(10'h1), .out(subtractor_1_out));  // open: bin, bout
  ROM #(.addrWidth(10), .dataWidth(9)) rom_1 (
    .addr(subtractor_1_out), .data({CmdIsRead, CorrectByteRead}));  // open: sel
  Comparator #(.mode("unsigned")) comparator_1 (
    .a(YourByteRead), .b(CorrectByteRead), .eq(comparator_1_eq));  // open: gt, lt
  and and_1 (Correct, comparator_1_eq, CmdIsRead);

  // Other names for the same wires on the sheet: Test_Number[9:0] = TestNumber

  // Notes on the sheet:
  //   Read Solutions
  //   contents of rom_1 (hex, n*v repeats v):
  //   1a3 1dc 6b 125 1 75 1dc 1c3 d8 1ab 77 70 b 33 10b d8 1c3 c9 174 58 bf 153 199 f 9d 56 1bb 13b 89 16c
  //   180 66 b6 0 e 107 1bf 1d8 167 89 118 55 1a2 e8 f2 1c3 d7 142 6b 73 1ab 18c 70 f da 1c3 14c 1d8 d5 4
  //   1d8 16b b1 1f4 1f2 ff 1da 50 1da 6d c2 f8 155 1c6 1f8 82 ae 1ff 35 d0 16b 1ae 72 175 3a 37 1ff 173
  //   1d0 158 167 1d5 96 a1 1f4 1c3 e6 cc 155 80 170 5d 1e6 166 e5 1ae 15 a2 ab 170 10f 13b 24 150 fc 33
  //   58 133 36 69 170 69 1c3 14c e4 80 e8 1ab 15d 158 1fc 135 cd 1e5 5a e0 104 73 8c 14c 68 99 ed 1a6
endmodule

module Set (
  input  Begin,
  input  [6:0] Tag,
  input  [1:0] Offset,
  input  [31:0] BlockFromMem,
  input  [7:0] CPUWriteVal,
  input  IsValid,
  input  IsDirty,
  input  IfTagChange,
  input  IfValidChange,
  input  IfDirtyChange,
  input  IfAgeChange,
  input  AgeIfEmpty,
  input  Write,
  input  CLK,
  output [6:0] UpdatedTag,
  output [31:0] UpdatedBlock,
  output [7:0] UpdatedByteRead,
  output UpdatedValid,
  output UpdatedDirty,
  output DidContain
);

  wire comparator_1_eq, comparator_2_eq, comparator_3_eq, comparator_4_eq, comparator_5_eq, comparator_6_eq,
       IfDirtyChange0, IfDirtyChange1, IfDirtyChange2, IfTagChange0, IfTagChange1, IfTagChange2,
       IfValidChange0, IfValidChange1, IfValidChange2, In0, In1, In2, or_2_out, UnprocessedDirty0,
       UnprocessedDirty1, UnprocessedDirty2, UnprocessedValid0, UnprocessedValid1, UnprocessedValid2, Write0,
       Write1, Write2;
  wire [1:0] BiggestOneIndex, multiplexer_1_out, multiplexer_2_out, multiplexer_3_out, multiplexer_4_out,
       multiplexer_5_out, NewAge0, NewAge1, NewAge2, Offest, target_block, UnprocessedAge0, UnprocessedAge1,
       UnprocessedAge2;
  wire [6:0] UnprocessedTag0, UnprocessedTag1, UnprocessedTag2;
  wire [7:0] UnprocessedRead0, UnprocessedRead1, UnprocessedRead2;
  wire [31:0] UnprocessedBlock0, UnprocessedBlock1, UnprocessedBlock2;

  Block block_1 (
    .Begin(Begin), .Tag(Tag), .Age(NewAge0), .Offset(Offest), .BlockFromMem(BlockFromMem),
    .CPUwriteVal(CPUWriteVal), .IsValid(IsValid), .IsDirty(IsDirty), .IfTagChange(IfTagChange0),
    .IfValidChange(IfValidChange0), .IfDirtyChange(IfDirtyChange0), .AgeChange(IfAgeChange), .Write(Write0),
    .CLK(CLK), .NewTag(UnprocessedTag0), .NewValid(UnprocessedValid0), .NewDirty(UnprocessedDirty0),
    .NewAge(UnprocessedAge0), .NewBlock(UnprocessedBlock0), .ByteRead(UnprocessedRead0));
  Block block_2 (
    .Begin(Begin), .Tag(Tag), .Age(NewAge1), .Offset(Offest), .BlockFromMem(BlockFromMem),
    .CPUwriteVal(CPUWriteVal), .IsValid(IsValid), .IsDirty(IsDirty), .IfTagChange(IfTagChange1),
    .IfValidChange(IfValidChange1), .IfDirtyChange(IfDirtyChange1), .AgeChange(IfAgeChange), .Write(Write1),
    .CLK(CLK), .NewTag(UnprocessedTag1), .NewValid(UnprocessedValid1), .NewDirty(UnprocessedDirty1),
    .NewAge(UnprocessedAge1), .NewBlock(UnprocessedBlock1), .ByteRead(UnprocessedRead1));
  Block block_3 (
    .Begin(Begin), .Tag(Tag), .Age(NewAge2), .Offset(Offest), .BlockFromMem(BlockFromMem),
    .CPUwriteVal(CPUWriteVal), .IsValid(IsValid), .IsDirty(IsDirty), .IfTagChange(IfTagChange2),
    .IfValidChange(IfValidChange2), .IfDirtyChange(IfDirtyChange2), .AgeChange(IfAgeChange), .Write(Write2),
    .CLK(CLK), .NewTag(UnprocessedTag2), .NewValid(UnprocessedValid2), .NewDirty(UnprocessedDirty2),
    .NewAge(UnprocessedAge2), .NewBlock(UnprocessedBlock2), .ByteRead(UnprocessedRead2));
  Comparator #(.width(2), .mode("unsigned")) comparator_1 (
    .a(UnprocessedAge2), .b(2'b10), .eq(comparator_1_eq));  // open: gt, lt
  Multiplexer #(.width(2), .enable("false")) multiplexer_1 (
    .in0(2'b10), .in1(2'b10), .out(multiplexer_1_out), .sel(In2));
  Comparator #(.width(7), .mode("unsigned")) comparator_2 (
    .a(UnprocessedTag0), .b(Tag), .eq(comparator_2_eq));  // open: gt, lt
  Comparator #(.width(7), .mode("unsigned")) comparator_3 (
    .a(UnprocessedTag1), .b(Tag), .eq(comparator_3_eq));  // open: gt, lt
  Multiplexer #(.width(2), .enable("false")) multiplexer_2 (
    .in0(2'b10), .in1(2'b10), .out(multiplexer_2_out), .sel(comparator_1_eq));
  and and_1 (In0, comparator_2_eq, UnprocessedValid0);
  and and_2 (In1, comparator_3_eq, UnprocessedValid1);
  Multiplexer #(.width(2), .enable("false")) multiplexer_3 (
    .in0(multiplexer_1_out), .in1(2'b01), .out(multiplexer_3_out), .sel(In1));
  Comparator #(.width(2), .mode("unsigned")) comparator_4 (
    .a(UnprocessedAge1), .b(2'b10), .eq(comparator_4_eq));  // open: gt, lt
  or or_1 (DidContain, In2, In1, In0);
  Multiplexer #(.width(2), .enable("false")) multiplexer_4 (
    .in0(multiplexer_2_out), .in1(2'b01), .out(multiplexer_4_out), .sel(comparator_4_eq));
  Multiplexer #(.width(2), .enable("false")) multiplexer_5 (
    .in0(multiplexer_3_out), .in1(2'b00), .out(multiplexer_5_out), .sel(In0));
  NextAge nextage_1 (
    .Age_Accessed(target_block), .Cur_Age0(UnprocessedAge0), .Cur_Age1(UnprocessedAge1),
    .Cur_Age2(UnprocessedAge2), .AgeIfEmpty(AgeIfEmpty), .NewAge0(NewAge0), .NewAge1(NewAge1),
    .NewAge2(NewAge2));
  or or_2 (or_2_out, In2, In1, In0);
  Comparator #(.width(2), .mode("unsigned")) comparator_5 (
    .a(UnprocessedAge0), .b(2'b10), .eq(comparator_5_eq));  // open: gt, lt
  Multiplexer #(.width(2), .enable("false")) multiplexer_6 (
    .in0(multiplexer_4_out), .in1(2'b00), .out(BiggestOneIndex), .sel(comparator_5_eq));
  Multiplexer #(.width(2), .enable("false")) multiplexer_7 (
    .in0(BiggestOneIndex), .in1(multiplexer_5_out), .out(target_block), .sel(or_2_out));
  Comparator #(.width(7), .mode("unsigned")) comparator_6 (
    .a(UnprocessedTag2), .b(Tag), .eq(comparator_6_eq));  // open: gt, lt
  and and_3 (In2, comparator_6_eq, UnprocessedValid2);
  Demultiplexer #(.select(2), .enable("false")) demultiplexer_1 (
    .out0(IfTagChange0), .out1(IfTagChange1), .out2(IfTagChange2), .in(IfTagChange), .sel(target_block));  // open: out3
  Demultiplexer #(.select(2), .enable("false")) demultiplexer_2 (
    .out0(IfDirtyChange0), .out1(IfDirtyChange1), .out2(IfDirtyChange2), .in(IfDirtyChange),
    .sel(target_block));  // open: out3
  Multiplexer #(.select(2), .width(7), .enable("false")) multiplexer_8 (
    .in0(UnprocessedTag0), .in1(UnprocessedTag1), .in2(UnprocessedTag2), .out(UpdatedTag), .sel(target_block));  // open: in3
  Multiplexer #(.select(2), .enable("false")) multiplexer_9 (
    .in0(UnprocessedValid0), .in1(UnprocessedValid1), .in2(UnprocessedValid2), .out(UpdatedValid),
    .sel(target_block));  // open: in3
  Multiplexer #(.select(2), .enable("false")) multiplexer_10 (
    .in0(UnprocessedDirty0), .in1(UnprocessedDirty1), .in2(UnprocessedDirty2), .out(UpdatedDirty),
    .sel(target_block));  // open: in3
  Multiplexer #(.select(2), .width(32), .enable("false")) multiplexer_11 (
    .in0(UnprocessedBlock0), .in1(UnprocessedBlock1), .in2(UnprocessedBlock2), .out(UpdatedBlock),
    .sel(target_block));  // open: in3
  Multiplexer #(.select(2), .width(8), .enable("false")) multiplexer_12 (
    .in0(UnprocessedRead0), .in1(UnprocessedRead1), .in2(UnprocessedRead2), .out(UpdatedByteRead),
    .sel(target_block));  // open: in3
  Demultiplexer #(.select(2), .enable("false")) demultiplexer_3 (
    .out0(IfValidChange0), .out1(IfValidChange1), .out2(IfValidChange2), .in(IfValidChange),
    .sel(target_block));  // open: out3
  Demultiplexer #(.select(2), .enable("false")) demultiplexer_4 (
    .out0(Write0), .out1(Write1), .out2(Write2), .in(Write), .sel(target_block));  // open: out3
endmodule

module Block (
  input  Begin,
  input  [6:0] Tag,
  input  [1:0] Age,
  input  [1:0] Offset,
  input  [31:0] BlockFromMem,
  input  [7:0] CPUwriteVal,
  input  IsValid,
  input  IsDirty,
  input  IfTagChange,
  input  IfValidChange,
  input  IfDirtyChange,
  input  AgeChange,
  input  Write,
  input  CLK,
  output [6:0] NewTag,
  output NewValid,
  output NewDirty,
  output [1:0] NewAge,
  output [31:0] NewBlock,
  output [7:0] ByteRead
);

  wire and_1_out, and_2_out, and_3_out, and_4_out, and_5_out, demultiplexer_1_out0, demultiplexer_1_out1,
       demultiplexer_1_out2, demultiplexer_1_out3;
  wire [7:0] multiplexer_1_out, multiplexer_2_out, multiplexer_3_out, multiplexer_4_out;

  and and_1 (and_1_out, Begin, Write);
  Demultiplexer #(.select(2), .enable("false")) demultiplexer_1 (
    .out0(demultiplexer_1_out0), .out1(demultiplexer_1_out1), .out2(demultiplexer_1_out2),
    .out3(demultiplexer_1_out3), .in(and_1_out), .sel(Offset));
  and and_2 (and_2_out, Begin, IfTagChange);
  Register #(.width(7)) State (.D(Tag), .en(and_2_out), .Q(NewTag), .clk(CLK));  // open: clr
  Register #(.width(1)) State_2 (.D(IsValid), .en(and_3_out), .Q(NewValid), .clk(CLK));  // open: clr
  and and_3 (and_3_out, Begin, IfValidChange);
  Register #(.width(1)) State_3 (.D(IsDirty), .en(and_4_out), .Q(NewDirty), .clk(CLK));  // open: clr
  and and_4 (and_4_out, Begin, IfDirtyChange);
  Register #(.width(2)) State_4 (.D(Age), .en(and_5_out), .Q(NewAge), .clk(CLK));  // open: clr
  and and_5 (and_5_out, Begin, AgeChange);
  Multiplexer #(.width(8), .enable("false")) multiplexer_1 (
    .in0(BlockFromMem[7:0]), .in1(CPUwriteVal), .out(multiplexer_1_out), .sel(demultiplexer_1_out0));
  Multiplexer #(.width(8), .enable("false")) multiplexer_2 (
    .in0(BlockFromMem[15:8]), .in1(CPUwriteVal), .out(multiplexer_2_out), .sel(demultiplexer_1_out1));
  Multiplexer #(.width(8), .enable("false")) multiplexer_3 (
    .in0(BlockFromMem[23:16]), .in1(CPUwriteVal), .out(multiplexer_3_out), .sel(demultiplexer_1_out2));
  Multiplexer #(.width(8), .enable("false")) multiplexer_4 (
    .in0(BlockFromMem[31:24]), .in1(CPUwriteVal), .out(multiplexer_4_out), .sel(demultiplexer_1_out3));
  Multiplexer #(.select(2), .width(8), .enable("false")) multiplexer_5 (
    .in0(NewBlock[7:0]), .in1(NewBlock[15:8]), .in2(NewBlock[23:16]), .in3(NewBlock[31:24]), .out(ByteRead),
    .sel(Offset));
  Register register_1 (.D(multiplexer_1_out), .en(demultiplexer_1_out0), .Q(NewBlock[7:0]), .clk(CLK));  // open: clr
  Register register_2 (.D(multiplexer_2_out), .en(demultiplexer_1_out1), .Q(NewBlock[15:8]), .clk(CLK));  // open: clr
  Register register_3 (.D(multiplexer_3_out), .en(demultiplexer_1_out2), .Q(NewBlock[23:16]), .clk(CLK));  // open: clr
  Register register_4 (.D(multiplexer_4_out), .en(demultiplexer_1_out3), .Q(NewBlock[31:24]), .clk(CLK));  // open: clr

  // Other names for the same wires on the sheet: FirstVal[7:0] = BlockFromMem[7:0];
  //   SecondVal[7:0] = BlockFromMem[15:8]; ThirdVal[7:0] = BlockFromMem[23:16]; FourthVal[7:0] = BlockFromMem[31:24];
  //   IfAgeChange = AgeChange
endmodule

module NextAge (
  input  [1:0] Age_Accessed,
  input  [1:0] Cur_Age0,
  input  [1:0] Cur_Age1,
  input  [1:0] Cur_Age2,
  input  AgeIfEmpty,
  output [1:0] NewAge0,
  output [1:0] NewAge1,
  output [1:0] NewAge2
);

  wire comparator_1_eq, comparator_1_gt, comparator_1_lt, comparator_2_eq, comparator_2_gt, comparator_2_lt,
       comparator_3_eq, comparator_3_gt, comparator_3_lt;
  wire [1:0] Add1Age0, Add1Age1, Add1Age2, Age_Accessed_t, multiplexer_1_out, multiplexer_2_out,
       multiplexer_3_out, multiplexer_5_out, multiplexer_6_out, multiplexer_7_out, New_Age0, New_Age1,
       New_Age2;

  Comparator #(.width(2), .mode("unsigned")) comparator_1 (
    .a(Cur_Age0), .b(Age_Accessed_t), .gt(comparator_1_gt), .eq(comparator_1_eq), .lt(comparator_1_lt));
  Comparator #(.width(2), .mode("unsigned")) comparator_2 (
    .a(Cur_Age1), .b(Age_Accessed_t), .gt(comparator_2_gt), .eq(comparator_2_eq), .lt(comparator_2_lt));
  Comparator #(.width(2), .mode("unsigned")) comparator_3 (
    .a(Cur_Age2), .b(Age_Accessed_t), .gt(comparator_3_gt), .eq(comparator_3_eq), .lt(comparator_3_lt));
  Multiplexer #(.width(2), .enable("false")) multiplexer_1 (
    .in0(Cur_Age0), .in1(2'b00), .out(multiplexer_1_out), .sel(comparator_1_eq));
  Multiplexer #(.width(2), .enable("false")) multiplexer_2 (
    .in0(Cur_Age1), .in1(2'b00), .out(multiplexer_2_out), .sel(comparator_2_eq));
  Multiplexer #(.width(2), .enable("false")) multiplexer_3 (
    .in0(Cur_Age2), .in1(2'b00), .out(multiplexer_3_out), .sel(comparator_3_eq));
  Multiplexer #(.select(2), .width(2), .enable("false")) multiplexer_4 (
    .in0(Cur_Age0), .in1(Cur_Age1), .in2(Cur_Age2), .out(Age_Accessed_t), .sel(Age_Accessed));  // open: in3
  Multiplexer #(.width(2), .enable("false")) multiplexer_5 (
    .in0(multiplexer_1_out), .in1(Add1Age0), .out(multiplexer_5_out), .sel(comparator_1_lt));
  Multiplexer #(.width(2), .enable("false")) multiplexer_6 (
    .in0(multiplexer_2_out), .in1(Add1Age1), .out(multiplexer_6_out), .sel(comparator_2_lt));
  Multiplexer #(.width(2), .enable("false")) multiplexer_7 (
    .in0(multiplexer_3_out), .in1(Add1Age2), .out(multiplexer_7_out), .sel(comparator_3_lt));
  Multiplexer #(.width(2), .enable("false")) multiplexer_8 (
    .in0(multiplexer_5_out), .in1(Cur_Age0), .out(New_Age0), .sel(comparator_1_gt));
  Multiplexer #(.width(2), .enable("false")) multiplexer_9 (
    .in0(multiplexer_6_out), .in1(Cur_Age1), .out(New_Age1), .sel(comparator_2_gt));
  Multiplexer #(.width(2), .enable("false")) multiplexer_10 (
    .in0(multiplexer_7_out), .in1(Cur_Age2), .out(New_Age2), .sel(comparator_3_gt));
  Adder #(.width(2)) adder_1 (.a(Cur_Age0), .b(2'b01), .out(Add1Age0));  // open: cin, cout
  Adder #(.width(2)) adder_2 (.a(Cur_Age1), .b(2'b01), .out(Add1Age1));  // open: cin, cout
  Adder #(.width(2)) adder_3 (.a(Cur_Age2), .b(2'b01), .out(Add1Age2));  // open: cin, cout
  Multiplexer #(.width(2), .enable("false")) multiplexer_11 (
    .in0(New_Age0), .in1(2'b00), .out(NewAge0), .sel(AgeIfEmpty));
  Multiplexer #(.width(2), .enable("false")) multiplexer_12 (
    .in0(New_Age1), .in1(2'b01), .out(NewAge1), .sel(AgeIfEmpty));
  Multiplexer #(.width(2), .enable("false")) multiplexer_13 (
    .in0(New_Age2), .in1(2'b10), .out(NewAge2), .sel(AgeIfEmpty));

  // Other names for the same wires on the sheet: Age_Accessed_index[1:0] = Age_Accessed
endmodule

module FSM (
  input  BIT2,
  input  BIT1,
  input  BIT0,
  input  Write,
  input  Read,
  input  Dirty,
  input  Found,
  output NextBit2,
  output NextBit1,
  output NextBit0,
  output Ready,
  output AgeIfEmpty,
  output CheckIfContainPreviously,
  output ReadFromMemory,
  output IfStore,
  output Write2Mem,
  output NewValid,
  output NewDirty
);

  wire and_1_out, and_2_out, and_3_out, and_4_out, and_5_out, and_6_out, and_7_out, and_8_out, and_9_out,
       and_10_out, and_11_out, and_12_out, and_16_out, and_17_out, and_18_out, and_19_out, and_20_out,
       and_22_out, and_23_out, not_1_out, not_2_out, not_3_out, not_4_out, not_5_out, not_6_out, not_7_out,
       not_8_out, not_9_out, not_10_out, not_11_out, not_12_out, not_13_out, not_14_out, not_15_out,
       not_16_out, not_17_out, not_18_out, not_19_out, not_20_out, not_21_out, not_22_out, not_23_out,
       not_24_out, not_25_out, not_26_out, not_27_out, not_28_out, not_29_out, not_30_out, not_31_out,
       not_32_out, not_33_out, not_34_out, not_35_out, not_36_out, not_37_out, not_38_out, not_39_out,
       not_40_out, not_41_out, not_42_out, not_43_out, not_44_out, not_45_out, not_46_out, not_47_out,
       not_48_out;

  not not_1 (not_1_out, BIT2);
  not not_2 (not_2_out, BIT1);
  not not_3 (not_3_out, BIT0);
  not not_4 (not_4_out, Read);
  not not_5 (not_5_out, BIT1);
  not not_6 (not_6_out, Read);
  not not_7 (not_7_out, BIT1);
  not not_8 (not_8_out, Write);
  not not_9 (not_9_out, BIT2);
  not not_10 (not_10_out, BIT0);
  not not_11 (not_11_out, BIT0);
  not not_12 (not_12_out, Read);
  not not_13 (not_13_out, BIT2);
  not not_14 (not_14_out, Read);
  not not_15 (not_15_out, Write);
  not not_16 (not_16_out, Found);
  not not_17 (not_17_out, Dirty);
  not not_18 (not_18_out, BIT2);
  not not_19 (not_19_out, BIT1);
  not not_20 (not_20_out, BIT2);
  not not_21 (not_21_out, BIT1);
  not not_22 (not_22_out, BIT0);
  not not_23 (not_23_out, BIT2);
  not not_24 (not_24_out, BIT0);
  not not_25 (not_25_out, BIT2);
  not not_26 (not_26_out, Found);
  not not_27 (not_27_out, Dirty);
  not not_28 (not_28_out, BIT1);
  not not_29 (not_29_out, BIT0);
  not not_30 (not_30_out, BIT2);
  not not_31 (not_31_out, BIT1);
  not not_32 (not_32_out, BIT0);
  not not_33 (not_33_out, BIT2);
  not not_34 (not_34_out, BIT1);
  not not_35 (not_35_out, Read);
  not not_36 (not_36_out, BIT2);
  not not_37 (not_37_out, BIT1);
  not not_38 (not_38_out, Write);
  not not_39 (not_39_out, BIT2);
  not not_40 (not_40_out, Found);
  not not_41 (not_41_out, BIT2);
  not not_42 (not_42_out, Found);
  not not_43 (not_43_out, Dirty);
  not not_44 (not_44_out, BIT1);
  not not_45 (not_45_out, BIT0);
  not not_46 (not_46_out, BIT0);
  not not_47 (not_47_out, Read);
  and and_1 (and_1_out, not_1_out, BIT1, BIT0);
  and and_2 (and_2_out, BIT2, not_2_out);
  and and_3 (and_3_out, BIT2, not_3_out, not_4_out);
  and and_4 (and_4_out, not_5_out, BIT0, not_6_out, Write);
  and and_5 (and_5_out, not_7_out, BIT0, Read, not_8_out);
  and and_6 (and_6_out, not_9_out, BIT1, not_10_out);
  and and_7 (and_7_out, BIT1, not_11_out, not_12_out);
  and and_8 (and_8_out, not_13_out, BIT1, Found);
  not not_48 (not_48_out, BIT0);
  and and_9 (and_9_out, not_14_out, not_15_out);
  and and_10 (and_10_out, Read, Write);
  and and_11 (and_11_out, BIT1, not_16_out, not_17_out);
  and and_12 (and_12_out, BIT2, BIT1);
  and and_13 (Ready, not_18_out, not_19_out, BIT0);
  and and_14 (AgeIfEmpty, not_20_out, not_21_out, not_22_out);
  and and_15 (CheckIfContainPreviously, not_23_out, BIT1, not_24_out);
  and and_16 (and_16_out, not_25_out, BIT1, BIT0, not_26_out, not_27_out);
  and and_17 (and_17_out, BIT2, not_28_out, not_29_out);
  and and_18 (and_18_out, not_30_out, not_31_out, not_32_out);
  and and_19 (and_19_out, not_33_out, not_34_out, not_35_out, Write);
  and and_20 (and_20_out, not_36_out, not_37_out, Read, not_38_out);
  and and_21 (Write2Mem, not_39_out, BIT1, BIT0, not_40_out, Dirty);
  and and_22 (and_22_out, not_41_out, BIT1, BIT0, not_42_out, not_43_out);
  and and_23 (and_23_out, BIT2, not_44_out, not_45_out);
  and and_24 (NewDirty, BIT2, BIT1, not_46_out, not_47_out);
  or or_1 (NextBit2, and_1_out, and_2_out, and_3_out);
  or or_2 (NextBit1, and_4_out, and_5_out, and_6_out, and_7_out, and_8_out);
  or or_3 (NextBit0, not_48_out, and_9_out, and_10_out, and_11_out, and_12_out);
  or or_4 (ReadFromMemory, and_16_out, and_17_out);
  or or_5 (IfStore, and_18_out, and_19_out, and_20_out);
  or or_6 (NewValid, and_22_out, and_23_out);
endmodule

module sfm0 (
  input  BIT2,
  input  BIT1,
  input  BIT0,
  input  Write,
  input  Read,
  input  Dirty,
  input  Found,
  output IfTagChange,
  output IfValidChange,
  output IfDirtyChange,
  output write_2,
  output newage
);

  wire and_1_out, and_2_out, and_3_out, and_4_out, and_5_out, and_6_out, and_7_out, and_8_out, and_9_out,
       and_10_out, and_11_out, and_12_out, not_1_out, not_2_out, not_3_out, not_4_out, not_5_out, not_6_out,
       not_7_out, not_8_out, not_9_out, not_10_out, not_11_out, not_12_out, not_13_out, not_14_out,
       not_15_out, not_16_out, not_17_out, not_18_out, not_19_out, not_20_out, not_21_out, not_22_out,
       not_23_out, not_24_out, not_25_out, not_26_out, not_27_out;

  not not_1 (not_1_out, BIT2);
  not not_2 (not_2_out, Found);
  not not_3 (not_3_out, Dirty);
  not not_4 (not_4_out, BIT1);
  not not_5 (not_5_out, BIT0);
  not not_6 (not_6_out, BIT2);
  not not_7 (not_7_out, Found);
  not not_8 (not_8_out, Dirty);
  not not_9 (not_9_out, BIT1);
  not not_10 (not_10_out, BIT0);
  not not_11 (not_11_out, BIT2);
  not not_12 (not_12_out, Found);
  not not_13 (not_13_out, Dirty);
  not not_14 (not_14_out, BIT1);
  not not_15 (not_15_out, BIT0);
  not not_16 (not_16_out, BIT0);
  not not_17 (not_17_out, Read);
  not not_18 (not_18_out, BIT2);
  not not_19 (not_19_out, Found);
  not not_20 (not_20_out, Dirty);
  not not_21 (not_21_out, BIT1);
  not not_22 (not_22_out, BIT0);
  not not_23 (not_23_out, BIT2);
  not not_24 (not_24_out, BIT1);
  not not_25 (not_25_out, BIT0);
  not not_26 (not_26_out, BIT2);
  not not_27 (not_27_out, BIT1);
  and and_1 (and_1_out, not_1_out, BIT1, BIT0, not_2_out, not_3_out);
  and and_2 (and_2_out, BIT2, not_4_out, not_5_out);
  and and_3 (and_3_out, not_6_out, BIT1, BIT0, not_7_out, not_8_out);
  and and_4 (and_4_out, BIT2, not_9_out, not_10_out);
  and and_5 (and_5_out, not_11_out, BIT1, BIT0, not_12_out, not_13_out);
  and and_6 (and_6_out, BIT2, not_14_out, not_15_out);
  and and_7 (and_7_out, BIT2, not_16_out, not_17_out);
  and and_8 (and_8_out, not_18_out, BIT1, BIT0, not_19_out, not_20_out);
  and and_9 (and_9_out, BIT2, not_21_out, not_22_out);
  and and_10 (and_10_out, not_23_out, not_24_out, not_25_out);
  and and_11 (and_11_out, not_26_out, BIT1, BIT0, Found);
  and and_12 (and_12_out, BIT2, not_27_out, BIT0);
  or or_1 (IfTagChange, and_1_out, and_2_out);
  or or_2 (IfValidChange, and_3_out, and_4_out);
  or or_3 (IfDirtyChange, and_5_out, and_6_out, and_7_out);
  or or_4 (write_2, and_8_out, and_9_out);
  or or_5 (newage, and_10_out, and_11_out, and_12_out);
endmodule
